# Fritzing sketch dijagram (saved by Fritzing 0.8.7b)
breadboards: 1

parts:
  MBED1 = mbed
  R1 = Rotary Potentiometer (Small) [maximum_resistance=100kΩ package=THT]
  R2 = Rotary Potentiometer (Small) [maximum_resistance=100kΩ package=THT]
  R3 = Rotary Potentiometer (Small) [maximum_resistance=100kΩ package=THT]
  R4 = Rotary Potentiometer (Small) [maximum_resistance=100kΩ package=THT]
  R5 = Rotary Potentiometer (Small) [maximum_resistance=100kΩ package=THT]
  R6 = Rotary Potentiometer (Small) [maximum_resistance=100kΩ package=THT]
  S1 = Pushbutton [package="[THT]"]
  S2 = Pushbutton [package="[THT]"]
  S3 = Pushbutton [package="[THT]"]
  S4 = Pushbutton [package="[THT]"]
  S5 = Pushbutton [package="[THT]"]
  S6 = Pushbutton [package="[THT]"]
  R8 = Resistor [tolerance=±5% resistance=220 package=THT]
  R9 = Resistor [tolerance=±5% resistance=220 package=THT]
  R10 = Resistor [tolerance=±5% resistance=220 package=THT]
  R11 = Resistor [tolerance=±5% resistance=220 package=THT]
  R12 = Resistor [tolerance=±5% resistance=220 package=THT]
  R13 = Resistor [tolerance=±5% resistance=220 package=THT]
  R14 = Resistor [tolerance=±5% resistance=220 package=THT]
  R15 = Resistor [tolerance=±5% resistance=220 package=THT]
  R16 = Resistor [tolerance=±5% resistance=220 package=THT]
  R17 = Resistor [tolerance=±5% resistance=220 package=THT]
  R18 = Resistor [tolerance=±5% resistance=220 package=THT]
  R19 = Resistor [tolerance=±5% resistance=220 package=THT]

nets:
  N1: MBED1.GND, R8.Pin_0, R9.Pin_0, R10.Pin_0, R11.Pin_0, R12.Pin_0, R13.Pin_0, R14.Pin_0, R15.Pin_0, R16.Pin_0, R17.Pin_0, R18.Pin_0, R19.Pin_0
  N2: MBED1.pin5, S1.Pin_1, R8.Pin_1
  N3: MBED1.pin6, S2.Pin_1, R9.Pin_1
  N4: MBED1.pin7, S3.Pin_1, S3.Pin_2, R10.Pin_1
  N5: MBED1.pin8, S4.Pin_1, S4.Pin_2, R11.Pin_1
  N6: MBED1.pin9, S5.Pin_1, R12.Pin_1
  N7: MBED1.pin10, S6.Pin_1, R13.Pin_1
  N8: MBED1.pin15, R1.wiper
  N9: MBED1.pin16, R2.wiper
  N10: MBED1.pin17, R3.wiper
  N11: MBED1.pin18, R4.wiper
  N12: MBED1.pin19, R5.wiper
  N13: MBED1.pin20, R6.wiper
  N14: MBED1.VOUT, R1.leg2, R2.leg2, R3.leg2, R4.leg2, R5.leg2, R6.leg2, S1.Pin_3, S1.Pin_4, S2.Pin_3, S2.Pin_4, S3.Pin_3, S3.Pin_4, S4.Pin_3, S4.Pin_4, S5.Pin_3, S6.Pin_3, S6.Pin_4
  N15: R1.leg1, R19.Pin_1
  N16: R2.leg1, R18.Pin_1
  N17: R3.leg1, R17.Pin_1
  N18: R4.leg1, R16.Pin_1
  N19: R5.leg1, R15.Pin_1
  N20: R6.leg1, R14.Pin_1
